// Logisim project ZCS.circ as structural Verilog
module alu (
  input  Carry_In,
  input  OE,
  input  [7:0] Accumulator,
  input  [7:0] Temp,
  input  [5:0] Operation,
  input  Carry_Usage,
  output [7:0] ALU_Out,
  output SF,
  output Carry_Out
);

  wire adder_1_cout, and_1_out, and_2_out, and_3_out, subtractor_1_bout;
  wire [7:0] adder_1_out, and_4_out, bus2buffercntrl_1_a_out, bus2buffercntrl_1_b_out,
       bus2buffercntrl_2_a_out, bus2buffercntrl_2_b_out, bus2buffercntrl_3_a_out, bus2buffercntrl_3_b_out,
       bus2buffercntrl_4_a_out, bus2buffercntrl_4_b_out, bus2buffercntrl_5_a_out, bus2buffercntrl_5_b_out,
       bus2buffercntrl_6_a_out, bus2buffercntrl_7_a_out, not_1_out, or_1_out, or_3_out, subtractor_1_out,
       xor_1_out;

  Bus2BufferCntrl bus2buffercntrl_1 (
    .A_Out(bus2buffercntrl_1_a_out), .B_Out(bus2buffercntrl_1_b_out), .A_In(Accumulator),
    .Control(Operation[0]), .B_In(Temp));
  Bus2BufferCntrl bus2buffercntrl_2 (
    .A_Out(bus2buffercntrl_2_a_out), .B_Out(bus2buffercntrl_2_b_out), .A_In(Accumulator),
    .Control(Operation[1]), .B_In(Temp));
  Bus2BufferCntrl bus2buffercntrl_3 (
    .A_Out(bus2buffercntrl_3_a_out), .B_Out(bus2buffercntrl_3_b_out), .A_In(Accumulator),
    .Control(Operation[2]), .B_In(Temp));
  Bus2BufferCntrl bus2buffercntrl_4 (
    .A_Out(bus2buffercntrl_4_a_out), .B_Out(bus2buffercntrl_4_b_out), .A_In(Accumulator),
    .Control(Operation[3]), .B_In(Temp));
  Bus2BufferCntrl bus2buffercntrl_5 (
    .A_Out(bus2buffercntrl_5_a_out), .B_Out(bus2buffercntrl_5_b_out), .A_In(Accumulator),
    .Control(Operation[4]), .B_In(Temp));
  Bus2BufferCntrl bus2buffercntrl_6 (
    .A_Out(bus2buffercntrl_6_a_out), .A_In(Accumulator), .Control(Operation[5]));  // open: B_Out, B_In
  and and_1 (and_1_out, Carry_Usage, Carry_In);
  and and_2 (and_2_out, Operation[0], and_1_out);
  and and_3 (and_3_out, Operation[1], and_1_out);
  Adder adder_1 (
    .a(bus2buffercntrl_1_a_out), .b(bus2buffercntrl_1_b_out), .out(adder_1_out), .cin(and_2_out),
    .cout(adder_1_cout));
  Subtractor subtractor_1 (
    .a(bus2buffercntrl_2_a_out), .b(bus2buffercntrl_2_b_out), .out(subtractor_1_out), .bin(and_3_out),
    .bout(subtractor_1_bout));
  assign and_4_out = bus2buffercntrl_3_a_out & bus2buffercntrl_3_b_out;  // AND_Gate and_4, 8 bits wide
  assign or_1_out = bus2buffercntrl_4_a_out | bus2buffercntrl_4_b_out;  // OR_Gate or_1, 8 bits wide
  assign xor_1_out = bus2buffercntrl_5_a_out ^ bus2buffercntrl_5_b_out;  // XOR_Gate xor_1, 8 bits wide
  assign not_1_out = ~bus2buffercntrl_6_a_out;  // NOT_Gate not_1, 8 bits wide
  Bus2BufferCntrl bus2buffercntrl_7 (
    .A_Out(bus2buffercntrl_7_a_out), .A_In(not_1_out), .Control(Operation[5]));  // open: B_Out, B_In
  or or_2 (Carry_Out, subtractor_1_bout, adder_1_cout);
  BusBufferCntrl busbuffercntrl_1 (.A_Out(ALU_Out), .A_In(or_3_out), .Control(OE));
  assign or_3_out = adder_1_out | subtractor_1_out | and_4_out | or_1_out | xor_1_out | bus2buffercntrl_7_a_out;  // OR_Gate or_3, 8 bits wide

  assign SF = OE;
endmodule

module prom (
  input  [12:0] AddressBus,
  input  MEMR,
  output [7:0] DataBus
);

  wire [7:0] rom_1_data;

  ROM #(.addrWidth(13)) rom_1 (.addr(AddressBus), .data(rom_1_data));
  and and_1 (DataBus[0], rom_1_data[0], MEMR);
  and and_2 (DataBus[1], rom_1_data[1], MEMR);
  and and_3 (DataBus[2], rom_1_data[2], MEMR);
  and and_4 (DataBus[3], rom_1_data[3], MEMR);
  and and_5 (DataBus[4], rom_1_data[4], MEMR);
  and and_6 (DataBus[5], rom_1_data[5], MEMR);
  and and_7 (DataBus[6], rom_1_data[6], MEMR);
  and and_8 (DataBus[7], rom_1_data[7], MEMR);
endmodule

module ram_mem (
  input  [12:0] AddressBus,
  input  WE,
  input  OE,
  input  CLK,
  output [7:0] DataBus
);

  RAM #(.addrWidth(13), .databus("bidir")) ram_1 (.addr(AddressBus), .we(WE), .oe(OE), .clk(CLK), .data(DataBus));
endmodule

module cpu (
);

  wire ALU_OE, ALUnit_carry_out, ALUnit_sf, ALUOP, and_1_out, and_2_out, and_3_out, AWE, c1_out, c2_out,
       clock_1_out, control_1_rom_oe, control_1_wm, dipswitch_1_p1, dipswitch_1_p2, FlagsFlipFlop_carry_out,
       HL_OE, HLT, INC_DEC, instructiondecoder_1_carryusage, IR_WE, JR, JS, LPC, LSP, MIr, MOV, MVMEM,
       not_1_out, PC_WE, PUSH, R_OE, R_WE, RMUXCTRL, RST, SP_PC, SP_WE, SPOP, TMP_OE, TMP_WE, ToMem,
       xor_1_out;
  wire [1:0] control_1_addrmux, count_1_cnt, FlagMux, instructiondecoder_1_add;
  wire [2:0] REGMUX, REGMUX_I;
  wire [3:0] FlagsFlipFlop_dout, undriven;
  wire [7:0] Accumulator_d_out, AIN, AOUT, instrreg_1_d_out, ram_1_data, rom_1_data, Temp_d_out, Temp_dout;
  wire [15:0] reg_mult_1_addrbus;

  Clock #(.highDuration(2), .lowDuration(2)) c1 (.out(c1_out));
  Clock #(.highDuration(2), .lowDuration(2), .phaseOffset(1)) c2 (.out(c2_out));
  regs Accumulator (.DOUT(AOUT), .D_Out(Accumulator_d_out), .OE(R_OE), .WE(AWE), .R(RST), .CLK(and_1_out), .DIN(AIN));
  not not_1 (not_1_out, HLT);
  and and_1 (and_1_out, not_1_out, c1_out);
  and and_2 (and_2_out, not_1_out, c2_out);
  Button button_1 (.out(RST));
  LED led_1 (.in(count_1_cnt[1]));
  count count_1 (.CNT(count_1_cnt), .CLK(and_2_out), .RST(RST));
  LED led_2 (.in(count_1_cnt[0]));
  regs Temp (.DOUT(Temp_dout), .D_Out(Temp_d_out), .OE(TMP_OE), .WE(TMP_WE), .R(RST), .CLK(and_1_out), .DIN(Temp_dout));
  // DipSwitch #(.number(3)) dipswitch_1: pin names not known; wires that end beside it: dipswitch_1_p1, dipswitch_1_p2, dipswitch_1_p1
  flags FlagsFlipFlop (
    .Carry_Out(FlagsFlipFlop_carry_out), .DOUT(FlagsFlipFlop_dout), .Carry_In(ALUnit_carry_out),
    .R(dipswitch_1_p2), .CLK(and_1_out), .WE(ALUnit_sf), .DIN(Temp_dout));
  alu ALUnit (
    .Carry_Out(ALUnit_carry_out), .ALU_Out(Temp_dout), .SF(ALUnit_sf), .Carry_In(FlagsFlipFlop_carry_out),
    .Operation({4'b0000, instructiondecoder_1_add}), .OE(ALU_OE), .Accumulator(Accumulator_d_out),
    .Temp(Temp_d_out), .Carry_Usage(instructiondecoder_1_carryusage));
  control control_1 (
    .C1(and_1_out), .C2(and_2_out), .EXC(count_1_cnt), .MIr(MIr), .LSP(LSP), .MOV(MOV), .MMOV(MVMEM),
    .ToMem(ToMem), .ALUOP(ALUOP), .REGMUX_I(REGMUX_I), .LPC(LPC), .JS(JS), .FALGS(undriven), .JR(JR),
    .FlagmMux(FlagMux), .SPOP(SPOP), .PUSH(PUSH), .AddrMux(control_1_addrmux), .IR_WE(IR_WE),
    .ROM_OE(control_1_rom_oe), .PC_WE(PC_WE), .SP_PC(SP_PC), .R_WE(R_WE), .TMP_OE(TMP_OE), .SP_WE(SP_WE),
    .TMP_WE(TMP_WE), .R_OE(R_OE), .RMUXCntrl(RMUXCTRL), .WM(control_1_wm), .ALU_OE(ALU_OE),
    .REGMUX_O(REGMUX), .HL_OE(HL_OE), .INC_DEC(INC_DEC));
  Clock clock_1 (.out(clock_1_out));
  InstrReg instrreg_1 (
    .D_Out(instrreg_1_d_out), .OE(1'b0), .WE(IR_WE), .R(RST), .CLK(and_1_out), .DIN(Temp_dout));  // open: DOUT
  // Digital_Oscilloscope digital_oscilloscope_1: pin names not known; wires that end beside it: clock_1_out, and_1_out, and_2_out
  InstructionDecoder instructiondecoder_1 (
    .InstructionReg(instrreg_1_d_out), .RMuxCtrl(RMUXCTRL), .RegMux(REGMUX_I), .HLT(HLT), .MIr(MIr),
    .LSP(LSP), .MOV(MOV), .ToMem(ToMem), .MVMEM(MVMEM), .ALUOP(ALUOP),
    .CarryUsage(instructiondecoder_1_carryusage), .Add(instructiondecoder_1_add[0]),
    .Sub(instructiondecoder_1_add[1]), .LPC(LPC), .JS(JS), .JR(JR), .FLAGMUX(FlagMux), .PUSH(PUSH),
    .SPOP(SPOP));
  xor xor_1 (xor_1_out, control_1_wm, reg_mult_1_addrbus[15]);
  and and_3 (and_3_out, xor_1_out, reg_mult_1_addrbus[15]);
  reg_mult reg_mult_1 (
    .DOUT(Temp_dout), .A_WE(AWE), .A_IN(AIN), .AddrBus(reg_mult_1_addrbus), .INC_DEC(INC_DEC), .OE(R_OE),
    .CLK(and_1_out), .WE(R_WE), .Reset(RST), .PC_WE(PC_WE), .DIN(Temp_dout), .HL_OE(HL_OE),
    .AddrMul(control_1_addrmux), .DataMUL(REGMUX), .A_OUT(AOUT), .SP_WE(SP_WE), .SP_PC(SP_PC));
  ROM #(.addrWidth(15)) rom_1 (.addr(reg_mult_1_addrbus[14:0]), .data(rom_1_data));
  RAM #(.addrWidth(15), .databus("bidir"), .trigger("high")) ram_1 (
    .addr(reg_mult_1_addrbus[14:0]), .we(control_1_wm), .oe(and_3_out), .data(ram_1_data));
  BusBufferCntrl busbuffercntrl_1 (.A_Out(Temp_dout), .A_In(rom_1_data), .Control(control_1_rom_oe));

  // Notes on the sheet:
  //   contents of rom_1 (hex, n*v repeats v):
  //   6 8 5 80 3f 1 69 4f ff 4 0 42 1 42 8a cc 0 42 ff
endmodule

module regs (
  input  OE,
  input  WE,
  input  R,
  input  [7:0] DIN,
  input  CLK,
  output [7:0] DOUT,
  output [7:0] D_Out
);

  Register register_1 (.D(DIN), .en(WE), .clk(CLK), .Q(D_Out), .clr(R));
  BusBufferCntrl busbuffercntrl_1 (.A_Out(DOUT), .A_In(D_Out), .Control(OE));
endmodule

module BusTrans (
  input  DIR_N,
  input  OE_N,
  input  [7:0] A,
  input  [7:0] B
);

  wire and_1_out, and_2_out;

  and and_1 (and_1_out, DIR_N, ~OE_N);  // AND_Gate
  assign B[0] = and_1_out ? A[0] : 1'bz;  // Controlled_Buffer controlled_buffer_1
  assign B[1] = and_1_out ? A[1] : 1'bz;  // Controlled_Buffer controlled_buffer_2
  assign B[2] = and_1_out ? A[2] : 1'bz;  // Controlled_Buffer controlled_buffer_3
  assign B[3] = and_1_out ? A[3] : 1'bz;  // Controlled_Buffer controlled_buffer_4
  assign B[4] = and_1_out ? A[4] : 1'bz;  // Controlled_Buffer controlled_buffer_5
  assign B[5] = and_1_out ? A[5] : 1'bz;  // Controlled_Buffer controlled_buffer_6
  assign B[6] = and_1_out ? A[6] : 1'bz;  // Controlled_Buffer controlled_buffer_7
  assign B[7] = and_1_out ? A[7] : 1'bz;  // Controlled_Buffer controlled_buffer_8
  and and_2 (and_2_out, ~DIR_N, ~OE_N);  // AND_Gate
  assign A[0] = and_2_out ? B[0] : 1'bz;  // Controlled_Buffer controlled_buffer_9
  assign A[1] = and_2_out ? B[1] : 1'bz;  // Controlled_Buffer controlled_buffer_10
  assign A[2] = and_2_out ? B[2] : 1'bz;  // Controlled_Buffer controlled_buffer_11
  assign A[3] = and_2_out ? B[3] : 1'bz;  // Controlled_Buffer controlled_buffer_12
  assign A[4] = and_2_out ? B[4] : 1'bz;  // Controlled_Buffer controlled_buffer_13
  assign A[5] = and_2_out ? B[5] : 1'bz;  // Controlled_Buffer controlled_buffer_14
  assign A[6] = and_2_out ? B[6] : 1'bz;  // Controlled_Buffer controlled_buffer_15
  assign A[7] = and_2_out ? B[7] : 1'bz;  // Controlled_Buffer controlled_buffer_16
endmodule

module LogicGate (
  input  Control,
  input  [7:0] B_In,
  input  [7:0] A_In,
  output [7:0] A_Out,
  output [7:0] B_Out
);

  and and_1 (A_Out[0], A_In[0], Control);
  and and_2 (B_Out[0], B_In[0], Control);
  and and_3 (A_Out[1], A_In[1], Control);
  and and_4 (B_Out[1], B_In[1], Control);
  and and_5 (A_Out[2], A_In[2], Control);
  and and_6 (B_Out[2], B_In[2], Control);
  and and_7 (A_Out[3], A_In[3], Control);
  and and_8 (B_Out[3], B_In[3], Control);
  and and_9 (A_Out[4], A_In[4], Control);
  and and_10 (B_Out[4], B_In[4], Control);
  and and_11 (A_Out[5], A_In[5], Control);
  and and_12 (B_Out[5], B_In[5], Control);
  and and_13 (A_Out[6], A_In[6], Control);
  and and_14 (B_Out[6], B_In[6], Control);
  and and_15 (A_Out[7], A_In[7], Control);
  and and_16 (B_Out[7], B_In[7], Control);
endmodule

module Bus2BufferCntrl (
  input  Control,
  input  [7:0] B_In,
  input  [7:0] A_In,
  output [7:0] A_Out,
  output [7:0] B_Out
);

  and and_1 (A_Out[0], A_In[0], Control);
  and and_2 (B_Out[0], B_In[0], Control);
  and and_3 (A_Out[1], A_In[1], Control);
  and and_4 (B_Out[1], B_In[1], Control);
  and and_5 (A_Out[2], A_In[2], Control);
  and and_6 (B_Out[2], B_In[2], Control);
  and and_7 (A_Out[3], A_In[3], Control);
  and and_8 (B_Out[3], B_In[3], Control);
  and and_9 (A_Out[4], A_In[4], Control);
  and and_10 (B_Out[4], B_In[4], Control);
  and and_11 (A_Out[5], A_In[5], Control);
  and and_12 (B_Out[5], B_In[5], Control);
  and and_13 (A_Out[6], A_In[6], Control);
  and and_14 (B_Out[6], B_In[6], Control);
  and and_15 (A_Out[7], A_In[7], Control);
  and and_16 (B_Out[7], B_In[7], Control);
endmodule

module BusBufferCntrl (
  input  Control,
  input  [7:0] A_In,
  output [7:0] A_Out
);

  assign A_Out[0] = Control ? A_In[0] : 1'bz;  // Controlled_Buffer controlled_buffer_1
  assign A_Out[1] = Control ? A_In[1] : 1'bz;  // Controlled_Buffer controlled_buffer_2
  assign A_Out[2] = Control ? A_In[2] : 1'bz;  // Controlled_Buffer controlled_buffer_3
  assign A_Out[3] = Control ? A_In[3] : 1'bz;  // Controlled_Buffer controlled_buffer_4
  assign A_Out[4] = Control ? A_In[4] : 1'bz;  // Controlled_Buffer controlled_buffer_5
  assign A_Out[5] = Control ? A_In[5] : 1'bz;  // Controlled_Buffer controlled_buffer_6
  assign A_Out[6] = Control ? A_In[6] : 1'bz;  // Controlled_Buffer controlled_buffer_7
  assign A_Out[7] = Control ? A_In[7] : 1'bz;  // Controlled_Buffer controlled_buffer_8
endmodule

module flags (
  input  Carry_In,
  input  R,
  input  CLK,
  input  WE,
  input  [7:0] DIN,
  output [3:0] DOUT,
  output Carry_Out
);

  wire and_1_out, and_2_out, and_3_out, and_4_out, and_5_out, and_6_out, and_7_out, and_8_out, and_9_out,
       or_1_out, or_2_out, or_3_out, or_4_out, undriven;
  wire [7:0] busbuffercntrl_1_a_out;

  and and_1 (and_1_out, ~busbuffercntrl_1_a_out[0], ~busbuffercntrl_1_a_out[1], ~busbuffercntrl_1_a_out[2], ~busbuffercntrl_1_a_out[3], ~busbuffercntrl_1_a_out[4], ~busbuffercntrl_1_a_out[5], ~busbuffercntrl_1_a_out[6], ~busbuffercntrl_1_a_out[7]);  // AND_Gate
  and and_2 (and_2_out, DOUT[0], ~WE);  // AND_Gate
  and and_3 (and_3_out, WE, and_1_out);
  and and_4 (and_4_out, DOUT[1], ~WE);  // AND_Gate
  and and_5 (and_5_out, WE, busbuffercntrl_1_a_out[7]);
  and and_6 (and_6_out, DOUT[2], ~WE);  // AND_Gate
  and and_7 (and_7_out, WE, ~busbuffercntrl_1_a_out[0]);  // AND_Gate
  and and_8 (and_8_out, Carry_Out, ~WE);  // AND_Gate
  and and_9 (and_9_out, WE, Carry_In);
  or or_1 (or_1_out, and_2_out, and_3_out);
  or or_2 (or_2_out, and_4_out, and_5_out);
  or or_3 (or_3_out, and_6_out, and_7_out);
  or or_4 (or_4_out, and_8_out, and_9_out);
  D_Flip_Flop ZERO (.D(or_1_out), .clk(CLK), .Q(DOUT[0]), .reset(undriven));  // open: Qn, preset
  D_Flip_Flop SIGN (.D(or_2_out), .clk(CLK), .Q(DOUT[1]), .reset(undriven));  // open: Qn, preset
  D_Flip_Flop PARITY (.D(or_3_out), .clk(CLK), .Q(DOUT[2]), .reset(R));  // open: Qn, preset
  D_Flip_Flop CARRY (.D(or_4_out), .clk(CLK), .Q(Carry_Out), .reset(R));  // open: Qn, preset
  BusBufferCntrl busbuffercntrl_1 (.A_Out(busbuffercntrl_1_a_out), .A_In(DIN), .Control(WE));

  assign DOUT[3] = Carry_Out;
endmodule

module InstructionDecoder (
  input  [7:0] InstructionReg,
  input  RMuxCtrl,
  output [2:0] RegMux,
  output HLT,
  output MIr,
  output LSP,
  output MOV,
  output ToMem,
  output MVMEM,
  output ALUOP,
  output CarryUsage,
  output Add,
  output Sub,
  output LPC,
  output JS,
  output JR,
  output [1:0] FLAGMUX,
  output PUSH,
  output SPOP
);

  wire and_2_out, and_6_out, and_11_out, and_12_out, and_13_out, demultiplexer_1_out0, demultiplexer_1_out1,
       demultiplexer_1_out2, demultiplexer_1_out3, nand_1_out, xor_1_out;
  wire [2:0] and_15_out, and_17_out, and_19_out, and_20_out, and_21_out, and_22_out, and_23_out, and_24_out,
       and_25_out, and_26_out, not_1_out, not_2_out;

  and and_1 (HLT, InstructionReg[0], InstructionReg[1], InstructionReg[2], InstructionReg[3], InstructionReg[4], InstructionReg[5], InstructionReg[6], InstructionReg[7]);
  nand nand_1 (nand_1_out, InstructionReg[0], InstructionReg[1], InstructionReg[2]);
  and and_2 (and_2_out, ~InstructionReg[3], ~InstructionReg[4], ~InstructionReg[5], ~InstructionReg[6], ~InstructionReg[7]);  // AND_Gate
  and and_3 (LSP, InstructionReg[0], InstructionReg[1], InstructionReg[2], InstructionReg[3], InstructionReg[4], InstructionReg[5], ~InstructionReg[6], ~InstructionReg[7]);  // AND_Gate
  and and_4 (MOV, InstructionReg[6], ~InstructionReg[7]);  // AND_Gate
  and and_5 (ToMem, InstructionReg[0], InstructionReg[1], InstructionReg[2]);
  and and_6 (and_6_out, InstructionReg[3], InstructionReg[4], InstructionReg[5]);
  and and_7 (ALUOP, ~InstructionReg[6], InstructionReg[7]);  // AND_Gate
  and and_8 (LPC, ~InstructionReg[0], ~InstructionReg[1], InstructionReg[2], ~InstructionReg[3], ~InstructionReg[4], InstructionReg[5], ~InstructionReg[6], ~InstructionReg[7]);  // AND_Gate
  and and_9 (JS, ~InstructionReg[0], ~InstructionReg[1], InstructionReg[2], InstructionReg[3], InstructionReg[6], InstructionReg[7]);  // AND_Gate
  and and_10 (JR, ~InstructionReg[0], ~InstructionReg[1], InstructionReg[2], ~InstructionReg[3], InstructionReg[6], InstructionReg[7]);  // AND_Gate
  and and_11 (and_11_out, InstructionReg[0], InstructionReg[1], InstructionReg[2]);
  and and_12 (and_12_out, InstructionReg[3], InstructionReg[4], InstructionReg[5]);
  and and_13 (and_13_out, ~InstructionReg[6], ~InstructionReg[7]);  // AND_Gate
  and and_14 (MIr, nand_1_out, and_2_out);
  assign and_15_out = {3{ALUOP}} & InstructionReg[5:3];  // AND_Gate and_15, 3 bits wide
  and and_16 (PUSH, and_11_out, ~and_12_out);  // AND_Gate
  assign and_17_out = InstructionReg[2:0] & {3{MIr}};  // AND_Gate and_17, 3 bits wide
  or or_1 (MVMEM, ToMem, and_6_out);
  assign not_1_out = ~{3{RMuxCtrl}};  // NOT_Gate not_1, 3 bits wide
  and and_18 (CarryUsage, ~InstructionReg[2], ALUOP, InstructionReg[0]);  // AND_Gate
  assign not_2_out = ~{3{PUSH}};  // NOT_Gate not_2, 3 bits wide
  assign and_19_out = {3{MOV}} & and_20_out;  // AND_Gate and_19, 3 bits wide
  assign and_20_out = InstructionReg[2:0] & {3{RMuxCtrl}};  // AND_Gate and_20, 3 bits wide
  assign and_21_out = {3{MOV}} & and_22_out;  // AND_Gate and_21, 3 bits wide
  assign and_22_out = not_1_out & InstructionReg[5:3];  // AND_Gate and_22, 3 bits wide
  Demultiplexer #(.select(3)) demultiplexer_1 (
    .out0(demultiplexer_1_out0), .out1(demultiplexer_1_out1), .out2(demultiplexer_1_out2),
    .out3(demultiplexer_1_out3), .in(ALUOP), .sel(InstructionReg[2:0]));  // open: out4, out5, out6, out7
  xor xor_1 (xor_1_out, and_11_out, and_12_out);
  assign and_23_out = {3{SPOP}} & and_24_out;  // AND_Gate and_23, 3 bits wide
  assign and_24_out = InstructionReg[2:0] & not_2_out;  // AND_Gate and_24, 3 bits wide
  assign and_25_out = {3{SPOP}} & and_26_out;  // AND_Gate and_25, 3 bits wide
  assign and_26_out = {3{PUSH}} & InstructionReg[5:3];  // AND_Gate and_26, 3 bits wide
  or or_2 (Add, demultiplexer_1_out0, demultiplexer_1_out1);
  or or_3 (Sub, demultiplexer_1_out2, demultiplexer_1_out3);
  and and_27 (SPOP, xor_1_out, and_13_out);
  assign RegMux = and_17_out | and_19_out | and_21_out | and_15_out | and_23_out | and_25_out;  // OR_Gate or_4, 3 bits wide

  assign FLAGMUX = InstructionReg[5:4];
endmodule

module reg_mult (
  input  [7:0] DIN,
  input  [2:0] DataMUL,
  input  [7:0] A_OUT,
  input  WE,
  input  OE,
  input  CLK,
  input  Reset,
  input  SP_WE,
  input  HL_OE,
  input  PC_WE,
  input  SP_PC,
  input  INC_DEC,
  input  [1:0] AddrMul,
  output [7:0] DOUT,
  output [7:0] A_IN,
  output A_WE,
  output [15:0] AddrBus
);

  wire demultiplexer_1_out1, demultiplexer_1_out2, demultiplexer_1_out3, demultiplexer_1_out4,
       demultiplexer_1_out5, demultiplexer_1_out6, not_1_out;
  wire [7:0] B_dout, C_dout, D_dout, demultiplexer_2_out1, demultiplexer_2_out2, demultiplexer_2_out3,
       demultiplexer_2_out4, demultiplexer_2_out5, demultiplexer_2_out6, hl_1_dout_h, hl_1_dout_l,
       multiplexer_2_out, regs_1_dout;
  wire [15:0] adder_1_out, controlled_buffer_1_out, hl_1_d_out, multiplexer_3_out, multiplexer_4_out,
       pc_1_d_out, stack_pointer_1_d_out;

  Demultiplexer #(.enable("true"), .select(3)) demultiplexer_1 (
    .out0(A_WE), .out1(demultiplexer_1_out1), .out2(demultiplexer_1_out2), .out3(demultiplexer_1_out3),
    .out4(demultiplexer_1_out4), .out5(demultiplexer_1_out5), .out6(demultiplexer_1_out6), .in(WE),
    .sel(DataMUL), .en(WE));  // open: out7
  Demultiplexer #(.enable("true"), .select(3), .width(8)) demultiplexer_2 (
    .out0(A_IN), .out1(demultiplexer_2_out1), .out2(demultiplexer_2_out2), .out3(demultiplexer_2_out3),
    .out4(demultiplexer_2_out4), .out5(demultiplexer_2_out5), .out6(demultiplexer_2_out6), .in(DIN),
    .sel(DataMUL), .en(WE));  // open: out7
  regs B (
    .DOUT(B_dout), .OE(OE), .WE(demultiplexer_1_out1), .R(Reset), .CLK(CLK), .DIN(demultiplexer_2_out1));  // open: D_Out
  regs D (
    .DOUT(D_dout), .OE(OE), .WE(demultiplexer_1_out3), .R(Reset), .CLK(CLK), .DIN(demultiplexer_2_out3));  // open: D_Out
  HL hl_1 (
    .DOUT_H(hl_1_dout_h), .DOUT_L(hl_1_dout_l), .D_Out(hl_1_d_out), .OE(OE), .R(Reset),
    .WE_H(demultiplexer_1_out5), .WE_L(demultiplexer_1_out6), .CLK(CLK), .DIN_H(demultiplexer_2_out5),
    .DIN_L(demultiplexer_2_out6));
  assign controlled_buffer_1_out = HL_OE ? hl_1_d_out : 16'bz;  // Controlled_Buffer controlled_buffer_1
  PC pc_1 (.D_Out(pc_1_d_out), .WE(PC_WE), .R(Reset), .CLK(CLK), .DIN(controlled_buffer_1_out));
  Multiplexer #(.select(2), .width(16)) multiplexer_1 (
    .in0(pc_1_d_out), .in1(stack_pointer_1_d_out), .in2(controlled_buffer_1_out), .out(AddrBus), .sel(AddrMul));  // open: in3
  Multiplexer #(.select(3), .width(8)) multiplexer_2 (
    .in0(A_OUT), .in1(B_dout), .in2(C_dout), .in3(D_dout), .in4(regs_1_dout), .in5(hl_1_dout_h),
    .in6(hl_1_dout_l), .out(multiplexer_2_out), .sel(DataMUL));  // open: in7
  regs C (
    .DOUT(C_dout), .OE(OE), .WE(demultiplexer_1_out2), .R(Reset), .CLK(CLK), .DIN(demultiplexer_2_out2));  // open: D_Out
  regs regs_1 (
    .DOUT(regs_1_dout), .OE(OE), .WE(demultiplexer_1_out4), .R(Reset), .CLK(CLK), .DIN(demultiplexer_2_out4));  // open: D_Out
  not not_1 (not_1_out, HL_OE);
  assign controlled_buffer_1_out = not_1_out ? adder_1_out : 16'bz;  // Controlled_Buffer controlled_buffer_2
  stack_pointer stack_pointer_1 (
    .D_Out(stack_pointer_1_d_out), .R(Reset), .WE(SP_WE), .CLK(CLK), .DIN(controlled_buffer_1_out));
  Multiplexer #(.width(16)) multiplexer_3 (
    .in0(stack_pointer_1_d_out), .in1(pc_1_d_out), .out(multiplexer_3_out), .sel(SP_PC));
  BusBufferCntrl busbuffercntrl_1 (.A_Out(DOUT), .A_In(multiplexer_2_out), .Control(OE));
  Multiplexer #(.width(16)) multiplexer_4 (.in0(16'h1), .in1({16{1'b1}}), .out(multiplexer_4_out), .sel(INC_DEC));
  Adder #(.width(16)) adder_1 (
    .a(multiplexer_3_out), .b(multiplexer_4_out), .out(adder_1_out), .cin(1'b0));  // open: cout
endmodule

module regs16 (
  input  OE,
  input  SELECTHL,
  input  [7:0] DIN,
  input  WE,
  input  R,
  input  CLK,
  output [7:0] DOUT,
  output [15:0] D_Out
);

  wire and_1_out, and_2_out, and_3_out, and_4_out;

  and and_1 (and_1_out, OE, SELECTHL);
  and and_2 (and_2_out, ~SELECTHL, OE);  // AND_Gate
  and and_3 (and_3_out, WE, SELECTHL);
  and and_4 (and_4_out, ~SELECTHL, WE);  // AND_Gate
  Register SPH (.D(DIN), .en(and_3_out), .clk(CLK), .Q(D_Out[15:8]), .clr(R));
  Register SPL (.D(DIN), .en(and_4_out), .clk(CLK), .Q(D_Out[7:0]), .clr(R));
  BusBufferCntrl busbuffercntrl_1 (.A_Out(DOUT), .A_In(D_Out[15:8]), .Control(and_1_out));
  BusBufferCntrl busbuffercntrl_2 (.A_Out(DOUT), .A_In(D_Out[7:0]), .Control(and_2_out));
endmodule

module stack_pointer (
  input  WE,
  input  [15:0] DIN,
  input  R,
  input  CLK,
  output [15:0] D_Out
);

  Register SPH (.D(DIN[15:8]), .en(WE), .clk(CLK), .Q(D_Out[15:8]), .clr(R));
  Register SPL (.D(DIN[7:0]), .en(WE), .clk(CLK), .Q(D_Out[7:0]), .clr(R));
endmodule

module HL (
  input  OE,
  input  [7:0] DIN_H,
  input  WE_H,
  input  WE_L,
  input  R,
  input  [7:0] DIN_L,
  input  CLK,
  output [7:0] DOUT_H,
  output [15:0] D_Out,
  output [7:0] DOUT_L
);

  Register H (.D(DIN_H), .en(WE_H), .clk(CLK), .Q(D_Out[15:8]), .clr(R));
  Register L (.D(DIN_L), .en(WE_L), .clk(CLK), .Q(D_Out[7:0]), .clr(R));
  BusBufferCntrl busbuffercntrl_1 (.A_Out(DOUT_H), .A_In(D_Out[15:8]), .Control(OE));
  BusBufferCntrl busbuffercntrl_2 (.A_Out(DOUT_L), .A_In(D_Out[7:0]), .Control(OE));
endmodule

module PC (
  input  [15:0] DIN,
  input  WE,
  input  R,
  input  CLK,
  output [15:0] D_Out
);

  Register #(.trigger("falling")) PCH (.D(DIN[15:8]), .en(WE), .clk(CLK), .Q(D_Out[15:8]), .clr(R));
  Register #(.trigger("falling")) PCL (.D(DIN[7:0]), .en(WE), .clk(CLK), .Q(D_Out[7:0]), .clr(R));
endmodule

module AddrBufCntrl (
  input  Control,
  input  [15:0] A_In,
  output [15:0] A_Out
);

  assign A_Out[15] = Control ? A_In[8] : 1'bz;  // Controlled_Buffer controlled_buffer_1
  assign A_Out[0] = Control ? A_In[0] : 1'bz;  // Controlled_Buffer controlled_buffer_2
  assign A_Out[14] = Control ? A_In[9] : 1'bz;  // Controlled_Buffer controlled_buffer_3
  assign A_Out[1] = Control ? A_In[1] : 1'bz;  // Controlled_Buffer controlled_buffer_4
  assign A_Out[13] = Control ? A_In[10] : 1'bz;  // Controlled_Buffer controlled_buffer_5
  assign A_Out[2] = Control ? A_In[2] : 1'bz;  // Controlled_Buffer controlled_buffer_6
  assign A_Out[12] = Control ? A_In[11] : 1'bz;  // Controlled_Buffer controlled_buffer_7
  assign A_Out[3] = Control ? A_In[3] : 1'bz;  // Controlled_Buffer controlled_buffer_8
  assign A_Out[11] = Control ? A_In[12] : 1'bz;  // Controlled_Buffer controlled_buffer_9
  assign A_Out[4] = Control ? A_In[4] : 1'bz;  // Controlled_Buffer controlled_buffer_10
  assign A_Out[10] = Control ? A_In[13] : 1'bz;  // Controlled_Buffer controlled_buffer_11
  assign A_Out[5] = Control ? A_In[5] : 1'bz;  // Controlled_Buffer controlled_buffer_12
  assign A_Out[9] = Control ? A_In[14] : 1'bz;  // Controlled_Buffer controlled_buffer_13
  assign A_Out[6] = Control ? A_In[6] : 1'bz;  // Controlled_Buffer controlled_buffer_14
  assign A_Out[8] = Control ? A_In[15] : 1'bz;  // Controlled_Buffer controlled_buffer_15
  assign A_Out[7] = Control ? A_In[7] : 1'bz;  // Controlled_Buffer controlled_buffer_16
endmodule

module count (
  input  CLK,
  input  RST,
  output [1:0] CNT
);

  wire and_1_out, j_k_ff_1_qn, or_1_out;

  or or_1 (or_1_out, RST, and_1_out);
  J_K_Flip_Flop j_k_ff_1 (
    .J(1'b1), .K(1'b1), .clk(CLK), .Q(CNT[0]), .Qn(j_k_ff_1_qn), .reset(or_1_out));  // open: preset
  J_K_Flip_Flop j_k_ff_2 (.J(1'b1), .K(1'b1), .clk(j_k_ff_1_qn), .Q(CNT[1]), .reset(or_1_out));  // open: Qn, preset
  and and_1 (and_1_out, CNT[0], CNT[1]);
endmodule

module control (
  input  C1,
  input  C2,
  input  [1:0] EXC,
  input  MIr,
  input  LSP,
  input  MOV,
  input  MMOV,
  input  ToMem,
  input  ALUOP,
  input  [2:0] REGMUX_I,
  input  LPC,
  input  JS,
  input  [3:0] FALGS,
  input  JR,
  input  [1:0] FlagmMux,
  input  SPOP,
  input  PUSH,
  output [1:0] AddrMux,
  output IR_WE,
  output ROM_OE,
  output PC_WE,
  output SP_PC,
  output R_WE,
  output TMP_OE,
  output SP_WE,
  output TMP_WE,
  output R_OE,
  output RMUXCntrl,
  output WM,
  output ALU_OE,
  output [2:0] REGMUX_O,
  output HL_OE,
  output INC_DEC
);

  wire and_1_out, and_3_out, and_4_out, and_5_out, and_6_out, and_7_out, and_8_out, and_9_out, and_10_out,
       and_12_out, and_13_out, and_15_out, and_16_out, and_17_out, and_18_out, and_21_out, and_22_out,
       and_23_out, and_24_out, and_26_out, and_27_out, and_28_out, bitselector_1_out, not_1_out, or_1_out;
  wire [0:0] not_2_out;
  wire [1:0] and_20_out, and_30_out, and_31_out;
  wire [1:1] and_11_out, nor_1_out, not_4_out;
  wire [2:2] not_3_out;

  BitSelector #(.width(4)) bitselector_1 (.in(FALGS), .out(bitselector_1_out), .sel(FlagmMux));
  and and_1 (and_1_out, ~EXC[0], EXC[1]);  // AND_Gate
  and and_2 (IR_WE, C2, and_3_out);
  and and_3 (and_3_out, C2, ~EXC[0], ~EXC[1]);  // AND_Gate
  and and_4 (and_4_out, ~C2, ~EXC[0], ~EXC[1]);  // AND_Gate
  and and_5 (and_5_out, EXC[0], ~EXC[1]);  // AND_Gate
  and and_6 (and_6_out, C2, and_7_out);
  and and_7 (and_7_out, MIr, and_5_out);
  and and_8 (and_8_out, ~C2, and_7_out);  // AND_Gate
  and and_9 (and_9_out, C2, and_10_out);
  and and_10 (and_10_out, LSP, and_1_out);
  and and_11 (and_11_out[1], MMOV, MOV);
  and and_12 (and_12_out, MOV, MMOV, and_5_out);
  and and_13 (and_13_out, ALUOP, C2, and_5_out);
  and and_14 (ALU_OE, ALUOP, and_1_out, C2);
  not not_1 (not_1_out, ALU_OE);
  assign REGMUX_O = not_1_out ? REGMUX_I : 3'bz;  // Controlled_Buffer controlled_buffer_1
  and and_15 (and_15_out, LPC, and_5_out, ~C2);  // AND_Gate
  and and_16 (and_16_out, JS, and_5_out, ~C2, bitselector_1_out);  // AND_Gate
  and and_17 (and_17_out, JR, and_5_out, ~C2, ~bitselector_1_out);  // AND_Gate
  and and_18 (and_18_out, SPOP, PUSH);
  // AND_Gate and_19 has open pins: in0=PUSH, in1=SPOP, out=open
  assign and_20_out = {2{and_11_out[1]}} & {and_11_out[1], not_2_out[0]};  // AND_Gate and_20, 2 bits wide
  not not_2 (not_2_out[0], and_11_out[1]);
  and and_21 (and_21_out, MOV, ~MMOV);  // AND_Gate
  and and_22 (and_22_out, and_12_out, ToMem);
  and and_23 (and_23_out, MMOV, ~ToMem, and_1_out);  // AND_Gate
  not not_3 (not_3_out[2], ALU_OE);
  assign REGMUX_O = ALU_OE ? {3{not_3_out[2]}} : 3'bz;  // Controlled_Buffer controlled_buffer_2
  or or_1 (or_1_out, and_15_out, and_16_out, and_17_out);
  and and_24 (and_24_out, and_5_out, C2, and_18_out);
  and and_25 (INC_DEC, and_18_out, C2, and_1_out);
  and and_26 (and_26_out, and_21_out, and_5_out);
  and and_27 (and_27_out, and_21_out, and_1_out);
  not not_4 (not_4_out[1], SPOP);
  nor nor_1 (nor_1_out[1], IR_WE, and_6_out);
  and and_28 (and_28_out, C2, and_26_out);
  and and_29 (TMP_OE, and_27_out, C2);
  assign and_30_out = {2{SPOP}} & {not_4_out[1], SPOP};  // AND_Gate and_30, 2 bits wide
  assign and_31_out = {2{nor_1_out[1]}} & and_20_out;  // AND_Gate and_31, 2 bits wide
  or or_2 (TMP_WE, and_28_out, and_13_out);
  assign AddrMux = and_31_out | and_30_out;  // OR_Gate or_3, 2 bits wide
  or or_4 (WM, and_22_out, and_24_out);
  or or_5 (ROM_OE, and_3_out, and_6_out);
  or or_6 (PC_WE, and_4_out, and_8_out, or_1_out);
  or or_7 (SP_PC, and_4_out, and_8_out, or_1_out, not_4_out[1]);
  or or_8 (R_WE, and_6_out, TMP_OE, and_23_out, ALU_OE);
  or or_9 (SP_WE, and_9_out, INC_DEC);
  or or_10 (R_OE, TMP_WE, WM);
  or or_11 (RMUXCntrl, TMP_OE, and_23_out);
  or or_12 (HL_OE, and_9_out, and_11_out[1], or_1_out);
endmodule

module InstrReg (
  input  OE,
  input  WE,
  input  R,
  input  [7:0] DIN,
  input  CLK,
  output [7:0] DOUT,
  output [7:0] D_Out
);

  Register register_1 (.D(DIN), .en(WE), .clk(CLK), .Q(D_Out), .clr(R));
  BusBufferCntrl busbuffercntrl_1 (.A_Out(DOUT), .A_In(D_Out), .Control(OE));
endmodule
